// Logisim project Memoria.circ as structural Verilog: 2 circuits, main circuit C3
module C3 (
  input  in_1,
  output [2:0] out_2
);

  wire d_ff_1_qn, d_ff_2_qn, d_ff_3_qn;

  D_Flip_Flop d_ff_1 (.clk(in_1), .D(d_ff_1_qn), .Q(out_2[0]), .Qn(d_ff_1_qn));  // open: preset, en, reset
  D_Flip_Flop d_ff_2 (.D(d_ff_2_qn), .Q(out_2[1]), .Qn(d_ff_2_qn));  // open: clk, preset, en, reset
  D_Flip_Flop d_ff_3 (.D(d_ff_3_qn), .Q(out_2[2]), .Qn(d_ff_3_qn));  // open: clk, preset, en, reset
endmodule

module Animador (
);

  wire [2:0] c3_1_out_2;
  wire [8:0] rom_1_data;

  C3 c3_1 (.out_2(c3_1_out_2));  // open: in_1
  ROM #(.addrWidth(3), .dataWidth(9)) rom_1 (.addr(c3_1_out_2), .data(rom_1_data));  // open: sel
  DotMatrix #(.matrixcols(3), .matrixrows(3)) dotmatrix_1 (
    .col0(rom_1_data[2:0]), .col1(rom_1_data[5:3]), .col2(rom_1_data[8:6]));
endmodule
